// Logisim project TraffictLight.circ as structural Verilog: 1 circuit, main circuit main
module main (
);

  wire and_1_out, and_2_out, and_3_out, and_4_out, and_5_out, and_6_out, and_7_out, button_1_out,
       button_2_out, button_3_out, clock_1_out, not_1_out, not_2_out, not_3_out, or_1_out, or_2_out,
       or_3_out, or_4_out, or_5_out, or_6_out, or_7_out, or_8_out, s_r_ff_1_q, s_r_ff_2_q, s_r_ff_3_q,
       shift_register_1_out, shift_register_1_q0, shift_register_1_q1, shift_register_1_q2,
       shift_register_1_q3, shift_register_2_out, shift_register_2_q0, shift_register_2_q1,
       shift_register_2_q2, shift_register_2_q3, shift_register_2_q4, shift_register_2_q5;

  Button button_1 (.out(button_1_out));
  Clock clock_1 (.out(clock_1_out));
  Button button_2 (.out(button_2_out));
  and and_1 (and_1_out, button_2_out, and_6_out);
  Shift_Register #(.length(4)) shift_register_1 (
    .in(and_2_out), .clk(clock_1_out), .out(shift_register_1_out), .clr(button_1_out),
    .q0(shift_register_1_q0), .q1(shift_register_1_q1), .q2(shift_register_1_q2), .q3(shift_register_1_q3));  // open: shift, load, d0, d1, d2, d3
  Button button_3 (.out(button_3_out));
  and and_2 (and_2_out, button_3_out, and_7_out);
  Shift_Register #(.length(6)) shift_register_2 (
    .in(and_1_out), .clk(clock_1_out), .out(shift_register_2_out), .clr(button_1_out),
    .q0(shift_register_2_q0), .q1(shift_register_2_q1), .q2(shift_register_2_q2), .q3(shift_register_2_q3),
    .q4(shift_register_2_q4), .q5(shift_register_2_q5));  // open: shift, load, d0, d1, d2, d3, d4, d5
  or or_1 (or_1_out, shift_register_1_q3, shift_register_1_q2, shift_register_1_q1, shift_register_1_q0);
  or or_2 (or_2_out, shift_register_1_out, button_1_out);
  or or_3 (or_3_out, button_1_out, shift_register_2_out);
  or or_4 (or_4_out, button_1_out, shift_register_1_out);
  not not_1 (not_1_out, shift_register_1_out);
  and and_3 (and_3_out, not_1_out, or_1_out);
  S_R_Flip_Flop s_r_ff_1 (
    .S(or_3_out), .clk(clock_1_out), .R(and_1_out), .Q(s_r_ff_1_q));  // open: Qn, preset, reset, en
  or or_5 (or_5_out, shift_register_2_q4, shift_register_2_q3, shift_register_2_q2, shift_register_2_q1, shift_register_2_q0);
  not not_2 (not_2_out, shift_register_1_out);
  S_R_Flip_Flop s_r_ff_2 (
    .S(or_2_out), .clk(clock_1_out), .R(and_1_out), .Q(s_r_ff_2_q));  // open: Qn, preset, reset, en
  or or_6 (or_6_out, s_r_ff_1_q, or_3_out);
  not not_3 (not_3_out, shift_register_2_q5);
  S_R_Flip_Flop s_r_ff_3 (
    .S(and_1_out), .clk(clock_1_out), .R(or_4_out), .Q(s_r_ff_3_q));  // open: Qn, preset, reset, en
  or or_7 (or_7_out, shift_register_1_out, s_r_ff_2_q);
  and and_4 (and_4_out, not_3_out, or_5_out);
  and and_5 (and_5_out, s_r_ff_3_q, not_2_out);
  and and_6 (and_6_out, or_7_out, or_6_out);
  or or_8 (or_8_out, and_4_out, and_3_out);
  and and_7 (and_7_out, or_6_out, and_5_out);
  LED led_1 (.in(and_6_out));
  LED led_2 (.in(or_8_out));
  LED led_3 (.in(and_7_out));

  // Notes on the sheet:
  //   RST
  //   LOCK
  //   UNLOCK
endmodule
