// Logisim project sum4bit.circ as structural Verilog: 2 circuits, main circuit main
module main (
  input  IN_CARRY,
  input  [3:0] IN_A,
  input  [3:0] IN_B,
  output [3:0] OUT_SUM,
  output OUT_CARRY
);

  wire helper_1_out_carry, helper_2_out_carry, helper_3_out_carry;

  helper helper_1 (.A(IN_B[0]), .B(IN_A[0]), .OUT(OUT_SUM[0]), .IN_CARRY(IN_CARRY), .OUT_CARRY(helper_1_out_carry));
  helper helper_2 (
    .A(IN_B[1]), .B(IN_A[1]), .OUT(OUT_SUM[1]), .IN_CARRY(helper_1_out_carry), .OUT_CARRY(helper_2_out_carry));
  helper helper_3 (
    .A(IN_B[2]), .B(IN_A[2]), .OUT(OUT_SUM[2]), .IN_CARRY(helper_2_out_carry), .OUT_CARRY(helper_3_out_carry));
  helper helper_4 (.A(IN_B[3]), .B(IN_A[3]), .OUT(OUT_SUM[3]), .IN_CARRY(helper_3_out_carry), .OUT_CARRY(OUT_CARRY));
endmodule

module helper (
  input  IN_CARRY,
  input  A,
  input  B,
  output OUT_CARRY,
  output OUT
);

  wire and_1_out, and_2_out, xor_1_out;

  xor xor_1 (xor_1_out, A, B);
  and and_1 (and_1_out, A, B);
  and and_2 (and_2_out, IN_CARRY, xor_1_out);
  xor xor_2 (OUT, IN_CARRY, xor_1_out);
  or or_1 (OUT_CARRY, and_1_out, and_2_out);
endmodule
